# Fritzing sketch Saber (saved by Fritzing 0.9.4)
stripboards: 1

parts:
  SPKR1 = Loudspeaker
  Q1 = Basic FET N-Channel [part_number=IRLML0060 package="TO220 [THT]"]
  Part1 = Mono 2.5W Class D Audio Amplifier - PAM8302
  Part2 = Adafruit Trinket M0 [part_number="Adafruit #3500"]
  Part6 = Lithium Ion Cylindrical Battery 3.7v 2200mAh [part_number=1781]
  Part7 = NeoPixel Stick [part_number=1426]
  S2 = Round Pushbutton
  U1 = Molex Picoblade Series Header [part_number=0532610519 package=Picoblade-53261-0519]
  U2 = Molex Picoblade Series Header [part_number=0532610519 package=Picoblade-53261-0519]
  R3 = Resistor [tolerance=±5% resistance=330 package="0603 [SMD]"]
  Part8 = Adafruit Pro Trinket LiIon/LiPoly Backpack [part_number="Adafruit #2124"]
  Part9 = Adafruit LIS3DH [part_number="Adafruit #2809"]

nets:
  N1: SPKR1.pin1, Part1.VO+
  N2: SPKR1.pin2, Part1.VO-
  N3: Q1.gate, R3.Pin_1
  N4: Q1.drain, Q1.source, Part7.GND, S2.leg1, U2.2
  GND: Part1.GND, Part2.GND, Part6.negative, U1.2, Part8.GND, Part9.GND
  VCC: Part1.VCC, Part2.VBAT, Part6.positive, U1.1, Part8.VBAT, Part9.VIN
  N5: Part1.SD, Part2.D3_A3_PA07_RXD_SCK, U1.3
  N6: Part1.AIN+, Part2.D1_A0_PA02
  N7: Part2.D4_A2_PA06_TXD_MOSI, U1.4
  N8: Part2.D2_A1_PA09_SCL_MISO, Part9.SCL
  N9: Part2.D0_A4_PA08_SDA, Part9.SDA
  N10: Part2.VBUS, Part8.VBUS
  N11: Part7.+5V, U2.1
  N12: Part7.DATAIN, U2.4
  N13: S2.leg0, U2.5
  N14: U2.3, R3.Pin_0

notes:
  Using SOT-23 Adafruit carrier baord with N-Channel Mosfet IRLML0060. 330R resistor.
  Neopixel Strip 84 pixels bent in half - 144 pixels per meter
  Battery can be plugged directly into charge board or on flying lead. Short the 500mA charge link! Standby power can be reduced further by removing charge LED.
  Parts List
  AdaFruit Trinket M0
  Adafruit 2.5W Audio Amp (2130)
  Adafruit Trinket LiPoly Backpack (2124)
  Adafruit SOT-23 breakout (1230)
  Adafruit Cylincrical Battery (1781)
  Adafruit Speaker Short Cable (4227)
  Adafruit LIS3DH Acceleromiter (2809)
  1 Meter 144 pixel Neopixel Strip
  Mosfet N-Channel IRLML0060 (RS 725-9341)
  Momentary Push Switch (RS 734-6735)
  PicoBlade 5 way M-F cable (RS 224-8717)
  PicoBlade 2 way F cable (RS 224-8481)
  330R Resistor
  Speaker can be connected using PicoBlade flying lead or using the long cable speaker soldered direct to audio amp. Adafruit long lead speaker is part no: 3923
  To reduce standby power to 400uA or less the following modifications are made:
  Dotstart LED removed from Trinket M0 (1.2mA quiesent)
  Green LED removed from Trinket M0 (0.3mA quiesent)
  Without these modifications power consumption in standby witll be around 2.0 to 2.5mA.

custom parts:
  Mono 2.5W Class D Audio Amplifier - PAM8302: A super small but powerful mono amplifier able to deliver up to 2.5 Watts into 4-8 ohm impedance speakers. Inside the miniature chip is a class D controller, able to run from 2.0V-5.5VDC. Since the amp is a class D, its very efficient (over 90% efficient when driving an 8Ω speaker at over half a Watt) - making it perfect for portable and battery-powered projects.
  Lithium Ion Cylindrical Battery 3.7v 2200mAh: This lithium ion battery has a capacity of 2200mAh and a protection circuit that provides over-voltage, under-voltage and over-current protection. This cell can provide 2C of peak current (4400mA). Note that these batteries are not designed to sustain such high loads, we suggest keeping any constant current draw under about 0.5C (1 Amp).
  NeoPixel Stick: Make your own little LED strip arrangement with this stick of NeoPixel LEDs. We crammed 8 of the tiny 5050 (5mm x 5mm) smart RGB LEDs onto a PCB with mounting holes and a chainable design. Use only one microcontroller pin to control as many as you can chain together! Each LED is addressable as the driver chip is inside the LED. Each one has ~18mA constant current drive so the color will be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
  Adafruit Pro Trinket LiIon/LiPoly Backpack: If you have a Pro Trinket you probably know it's the perfect little size for a portable project. This LiPoly backpack makes it really easy to do! Instead of wiring 2 or 3 boards together to make a charging system, this little PCB sits on top of the Pro Trinket and allows a LiPoly/LiIon battery to plug in. When the Pro Trinket USB port is powered, the battery is recharged automatically. Unplug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
  Adafruit LIS3DH: The LIS3DH is a very popular low power triple-axis accelerometer. It's low-cost, but has just about every 'extra' you'd want in an accelerometer: Three axis sensing, 10-bit precision ±2g/±4g/±8g/±16g selectable scaling Both I2C (2 possible addresses) and SPI interface options Interrupt output Multiple data rate options 1 Hz to 5Khz As low as 2uA current draw (just the chip itself, not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
